# Fritzing sketch relay (saved by Fritzing 0.9.2b)
breadboards: 1

parts:
  R1 = Resistor [tolerance=±5% resistance=220 package=THT]
  R2 = Resistor [tolerance=±5% resistance=220 package=THT]
  LED2 = LED - 5mm [color="Red (633nm)" package="5 mm [THT]"]
  LED3 = LED - 5mm [color="Red (633nm)" package="5 mm [THT]"]
  U1 = RELAY [package=relay-jzc]
  U2 = RELAY [package=relay-jzc]
  元件1 = Arduino Uno (Rev3)

nets:
  N1: R1.Pin_0, LED3.anode
  N2: R1.Pin_1, R2.Pin_1, U2.MAIN, 元件1.5V
  N3: R2.Pin_0, LED2.anode
  N4: LED2.cathode, U2.NC
  N5: LED3.cathode, U1.NC
  N6: U1.COIL2, U2.COIL2, U2.COIL1, 元件1.GND
  N7: U1.MAIN, 元件1.D9_PWM
  N8: U1.COIL1, 元件1.D8

notes:
  IN2 IN1 GND VCC
